// Digital circuit CPU.dig as structural Verilog
module CPU (
  input  clk,
  input  clk_2,
  input  [31:0] Interface
);

  wire button_1_out, button_2_out, Clk_t, CopyClk, counter_1_ovf, Ctrl_Alloc, Ctrl_AllocOut, Ctrl_Dealloc,
       Ctrl_InterfaceOut, Ctrl_MemAdrIn, Ctrl_MemOut, Ctrl_MemRevOut, dipswitch_1_out, dipswitch_2_out,
       multiplexer_1_out, or_2_out;
  wire [3:0] multiplexer_3_out, multiplexer_3_out_2, multiplexer_3_out_3, multiplexer_3_out_4,
       multiplexer_3_out_5;
  wire [15:0] mmu_1_p5, mmu_1_p5_2;
  wire [23:0] counter_1_out, mmu_1_p6, mmu_1_p8, mmu_1_p9, multiplexer_4_out, multiplexer_5_out, not_1_out;
  wire [23:20] multiplexer_3_out_6;
  wire [31:0] Bus;

  not not_1 (not_1_out[0], mmu_1_p6[0]);
  // MMU mmu_1: pin names not known; wires that end beside it: Ctrl_Alloc, Ctrl_Dealloc, Ctrl_AllocOut, Bus, {mmu_1_p5_2, mmu_1_p5}, mmu_1_p6, {mmu_1_p5_2, mmu_1_p5}, mmu_1_p8, mmu_1_p9
  Button button_1 (.out(button_1_out));
  Multiplexer multiplexer_1 (.sel(dipswitch_1_out), .in_0(button_1_out), .in_1(clk), .out(multiplexer_1_out));
  DipSwitch dipswitch_1 (.out(dipswitch_1_out));
  Counter #(.Bits(24)) counter_1 (.en(not_1_out[0]), .C(CopyClk), .clr(1'b0), .out(counter_1_out), .ovf(counter_1_ovf));
  Button button_2 (.out(button_2_out));
  Multiplexer multiplexer_2 (.sel(dipswitch_2_out), .in_0(button_2_out), .in_1(clk_2), .out(Clk_t));
  DipSwitch dipswitch_2 (.out(dipswitch_2_out));
  and and_1 (CopyClk, multiplexer_1_out, not_1_out[0]);
  or or_1 (mmu_1_p6[0], mmu_1_p6[0], counter_1_ovf);
  Multiplexer #(.Bits(24)) multiplexer_3 (
    .sel(mmu_1_p6[0]), .in_0(counter_1_out), .in_1(mmu_1_p6),
    .out({multiplexer_3_out_6, multiplexer_3_out_5, multiplexer_3_out_4, multiplexer_3_out_3, multiplexer_3_out_2, multiplexer_3_out}));
  Multiplexer #(.Bits(24)) multiplexer_4 (
    .sel(mmu_1_p6[0]), .in_0(not_1_out), .in_1(mmu_1_p8), .out(multiplexer_4_out));
  Multiplexer #(.Bits(24)) multiplexer_5 (
    .sel(mmu_1_p6[0]), .in_0(not_1_out), .in_1(mmu_1_p9), .out(multiplexer_5_out));
  ROM #(.bigEndian("true"), .AddrBits(24), .Bits(32)) Boot (
    .A({multiplexer_3_out_6, multiplexer_3_out_5, multiplexer_3_out_4, multiplexer_3_out_3, multiplexer_3_out_2, multiplexer_3_out}),
    .sel(not_1_out[0]), .D({mmu_1_p5_2, mmu_1_p5}));
  RAMSinglePort #(.AddrBits(24), .Bits(32)) ramsingleport_1 (
    .A({multiplexer_3_out_6, multiplexer_3_out_5, multiplexer_3_out_4, multiplexer_3_out_3, multiplexer_3_out_2, multiplexer_3_out}),
    .str(multiplexer_4_out[0]), .C(CopyClk), .ld(multiplexer_5_out[0]), .D({mmu_1_p5_2, mmu_1_p5}));
  Seven_Seg_Hex seven_seg_hex_1 (.d(multiplexer_3_out_6), .dp(1'b0));
  Seven_Seg_Hex seven_seg_hex_2 (.d(multiplexer_3_out_5), .dp(1'b0));
  Seven_Seg_Hex seven_seg_hex_3 (.d(multiplexer_3_out_4), .dp(1'b0));
  or or_2 (or_2_out, Ctrl_MemOut, not_1_out[0]);
  Seven_Seg_Hex seven_seg_hex_4 (.d(multiplexer_3_out_3), .dp(1'b0));
  assign Bus = or_2_out ? {mmu_1_p5_2, mmu_1_p5} : 32'bz;  // Driver driver_1
  assign Bus = Ctrl_MemRevOut ? {mmu_1_p5, mmu_1_p5_2} : 32'bz;  // Driver driver_2
  assign Bus = Ctrl_InterfaceOut ? Interface : 32'bz;  // Driver driver_3
  Seven_Seg_Hex seven_seg_hex_5 (.d(multiplexer_3_out_2), .dp(1'b0));
  Seven_Seg_Hex seven_seg_hex_6 (.d(multiplexer_3_out), .dp(1'b0));
  Seven_Seg_Hex seven_seg_hex_7 (.d(Bus[31:28]), .dp(1'b0));
  DipSwitch dipswitch_3 (.out(Ctrl_MemOut));
  DipSwitch dipswitch_4 (.out(Ctrl_MemRevOut));
  DipSwitch dipswitch_5 (.out(Ctrl_MemAdrIn));
  DipSwitch dipswitch_6 (.out(Ctrl_InterfaceOut));
  DipSwitch dipswitch_7 (.out(Ctrl_Alloc));
  DipSwitch dipswitch_8 (.out(Ctrl_Dealloc));
  DipSwitch dipswitch_9 (.out(Ctrl_AllocOut));
  Seven_Seg_Hex seven_seg_hex_8 (.d(Bus[27:24]), .dp(1'b0));
  Seven_Seg_Hex seven_seg_hex_9 (.d(Bus[23:20]), .dp(1'b0));
  Seven_Seg_Hex seven_seg_hex_10 (.d(Bus[19:16]), .dp(1'b0));
  Seven_Seg_Hex seven_seg_hex_11 (.d(Bus[15:12]), .dp(1'b0));
  Seven_Seg_Hex seven_seg_hex_12 (.d(Bus[11:8]), .dp(1'b0));
  Seven_Seg_Hex seven_seg_hex_13 (.d(Bus[7:4]), .dp(1'b0));
  Seven_Seg_Hex seven_seg_hex_14 (.d(Bus[3:0]), .dp(1'b0));
  // Pins of 1 and 24 bits meet at not_1_out
  // Pins of 1 and 24 bits meet at mmu_1_p6
  // Pins of 1 and 24 bits meet at multiplexer_4_out
  // Pins of 1 and 24 bits meet at multiplexer_5_out

  // Notes on the sheet:
  //   clk: Hz: 2147483647
  //   clk_2: Hz: 10
  //   Memory Address
  //   Boot loads boot.spy
  //   Bus
endmodule
