// Digital circuit MMU.dig as structural Verilog
module MMU (
  input  Ctrl_Alloc,
  input  Ctrl_Dealloc,
  input  Ctrl_AllocOut,
  input  [31:0] Bus,
  input  [31:0] MemDataIn,
  output [23:0] MemAddr,
  output [31:0] MemDataOut,
  output MemStr,
  output MemLd
);

  wire Step_ovf;
  wire [2:0] State_q, Step_out;

  Register #(.Bits(3)) State (.Q(State_q));  // open: D, C, en
  Counter #(.Bits(3)) Step (.clr(Step_ovf), .out(Step_out), .ovf(Step_ovf));  // open: en, C
  ROM #(.AddrBits(6), .Bits(8)) Microcode (.A({State_q, Step_out}));  // open: sel, D
  Driver driver_1 (.out(MemDataOut[0]));  // open: in, en
  // Pins of 1 and 32 bits meet at MemDataOut

  // Notes on the sheet:
  //   Microcode loads MMU_Opcode.bin
endmodule
